// Logisim project d-latch2.circ as structural Verilog: 1 circuit, main circuit main
module main (
  input  in_1,
  input  in_2,
  output out_3,
  output out_4
);

  wire nand_1_out, nand_2_out, not_1_out;

  not not_1 (not_1_out, in_1);
  nand nand_1 (nand_1_out, not_1_out, in_2);
  nand nand_2 (nand_2_out, in_2, in_1);
  nand nand_3 (out_4, out_3, nand_2_out);
  nand nand_4 (out_3, nand_1_out, out_4);
endmodule
